# Fritzing sketch CC1101Board2 (saved by Fritzing 0.9.10b)
circuit board: 6.4cm x 2.5cm
breadboards: 1

parts:
  J4 = double row female pin header, 8 pins [form="♀ (female)"]
  J3 = double row female pin header, 8 pins [form="♀ (female)"]
  J6 = female pin header, 8 pins [form="♀ (female)"]
  J5 = female pin header, 8 pins [form="♀ (female)"]
  J7 = female pin header, 10 pins [form="♀ (female)"]
  J8 = female pin header, 10 pins [form="♀ (female)"]

nets:
  N1: J4.pin1, J3.pin5, J7.pin1, J8.pin1
  N2: J4.pin2, J3.pin2, J6.pin5, J5.pin5
  N3: J4.pin4, J3.pin6, J6.pin4, J5.pin4
  N4: J4.pin5, J3.pin3, J6.pin6, J5.pin6
  N5: J4.pin6, J3.pin1, J6.pin3, J5.pin3
  N6: J4.pin7, J3.pin7, J6.pin2, J5.pin2
  N7: J4.pin8, J3.pin4, J6.pin8, J5.pin8

notes:
  Flipper Zero
  CC1101 SubGHZ
